# Fritzing sketch fritzing layout (saved by Fritzing 0.9.3b)
stripboards: 1

parts:
  Pololu_DRV1 = Pololu DRV8801 [package=SO16]
  Adafruit_HUZZAH_ESP8266_Breakout2 = Adafruit HUZZAH ESP8266 Breakout [part_number=2471]
  J3 = screw terminal, 3 pins
  J4 = male pin header, 2 pins [form="♂ (male)"]
  J5 = male pin header, 5 pins [form="♂ (male)"]
  J6 = screw terminal, 3 pins
  Part1 = Triple Axis Accelerometer Breakout - ADXL345
  J7 = male pin header, 5 pins [form="♂ (male)"]
  R1 = Resistor [tolerance=±5% resistance=1k package=THT]
  R2 = Resistor [tolerance=±5% resistance=1M package=THT]
  R3 = Resistor [tolerance=±5% resistance=150k package=THT]

nets:
  VDD: Pololu_DRV1.VDD, Adafruit_HUZZAH_ESP8266_Breakout2.3V, J5.pin2, Part1.VCC
  N1: Pololu_DRV1.SLEEP, Adafruit_HUZZAH_ESP8266_Breakout2.#16, R1.Pin_0
  N2: Pololu_DRV1.DIR, Adafruit_HUZZAH_ESP8266_Breakout2.#2
  N3: Pololu_DRV1.PWM, Adafruit_HUZZAH_ESP8266_Breakout2.#15
  GND: Pololu_DRV1.GND#5, Adafruit_HUZZAH_ESP8266_Breakout2.GND, J4.pin1, J5.pin1, Part1.GND, J7.pin5, R1.Pin_1, R3.Pin_1
  N4: Pololu_DRV1.CS, R2.Pin_0
  N5: Pololu_DRV1.VMM, J3.pin1
  N6: Pololu_DRV1.OUT+, J6.pin1
  N7: Pololu_DRV1.OUT-, J6.pin3
  N8: Pololu_DRV1.GND#12, J3.pin3
  N9: Adafruit_HUZZAH_ESP8266_Breakout2.VBat, J4.pin2
  N10: Adafruit_HUZZAH_ESP8266_Breakout2.#13, J7.pin1
  N11: Adafruit_HUZZAH_ESP8266_Breakout2.#12, J7.pin2
  N12: Adafruit_HUZZAH_ESP8266_Breakout2.#14, J7.pin3
  N13: Adafruit_HUZZAH_ESP8266_Breakout2.A, R2.Pin_1, R3.Pin_0
  N14: Adafruit_HUZZAH_ESP8266_Breakout2.RST, J7.pin4
  N15: Adafruit_HUZZAH_ESP8266_Breakout2.#5, J5.pin5, Part1.SDA
  N16: Adafruit_HUZZAH_ESP8266_Breakout2.#4, J5.pin4, Part1.SCL
  N17: Adafruit_HUZZAH_ESP8266_Breakout2.#0, J5.pin3, Part1.CS

custom parts:
  Pololu DRV8801: This tiny breakout board for TI’s DRV8801 provides a modern alternative to classic motor drivers such as the L293D, SN754410, and L298N. It can deliver a continuous 1 A (2.8 A peak) to a single motor and offers a wide operating voltage range of 8 V to 36 V. The DRV8801 features a simple two-pin speed/direction interface, current-sense feedback, and built-in protection against under-voltage,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
